# Fritzing sketch circuit02 (saved by Fritzing 0.7.10b)
perfboards: 1

parts:
  R2 = Resistor [tolerance=±5% resistance=220 package=THT]  # not connected
  R3 = Resistor [tolerance=±5% resistance=220 package=THT]  # not connected
  R4 = Resistor [tolerance=±5% resistance=220 package=THT]  # not connected
  S1 = Pushbutton [package="[THT]"]
  R1 = Rotary Potentiometer (Small) [maximum_resistance=10kΩ]  # not connected
  LED2 = RGB LED - (4 legs) [package="5 mm [THT]"]  # not connected
  U1 = mystery part, 2 pins [chip_label=?]  # not connected
  U3 = mystery part, 16 pins [chip_label=?]
  U4 = mystery part, 16 pins [chip_label=?]
  S2 = Pushbutton [package="[THT]"]
  Arduino1 = Arduino  # not connected

nets:
  N1: S1.Pin_1, S1.Pin_2
  N2: S1.Pin_3, S1.Pin_4
  N3: U3.pin3, U3.pin4, U3.pin5, U3.pin16
  N4: U3.pin9, U4.pin5
  N5: U3.pin10, U4.pin3
  N6: U3.pin11, U4.pin13
  N7: U3.pin12, U4.pin16
  N8: U3.pin13, U4.pin14
  N9: U3.pin14, U4.pin15
  N10: U3.pin15, U4.pin11
  N11: S2.Pin_1, S2.Pin_2
  N12: S2.Pin_3, S2.Pin_4
