# Fritzing sketch circuitproject01 (saved by Fritzing 0.7.10b)
breadboards: 1

parts:
  arduino = Arduino
  R1 = Resistor [tolerance=±5% package=1_6w-res]  # not connected
  LED4 = LED - 5mm [color="Green (570nm)" package="5 mm [THT]"]
  LED5 = LED - 5mm [color="Yellow (595nm)" package="5 mm [THT]"]
  R6 = Resistor [tolerance=±5% resistance=330 package=THT]
  R8 = Resistor [tolerance=±5% resistance=330 package=THT]
  R9 = Resistor [tolerance=±5% resistance=330 package=THT]
  LED6 = LED - 5mm [color="Red (633nm)" package="5 mm [THT]"]
  SG1 = Buzzer 12mm [package=buzzer-12mm]  # not connected
  J1 = Piezo Speaker

nets:
  N1: arduino.GND, R6.Pin_0, R8.Pin_0, R9.Pin_0, J1.pin1
  N2: arduino.D11, LED6.anode
  N3: arduino.D10, LED5.anode
  N4: arduino.D9, LED4.anode
  N5: arduino.D6, J1.pin2
  N6: LED4.cathode, R9.Pin_1
  N7: LED5.cathode, R6.Pin_1
  N8: R8.Pin_1, LED6.cathode

notes:
  buzzer
